# Fritzing sketch FINAL-PROJECT (saved by Fritzing 0.8.7b)
breadboards: 1

parts:
  R1 = Resistor [tolerance=±5% resistance=32 package=THT]
  R2 = Resistor [tolerance=±5% resistance=22k package=THT]
  C1 = Tantalum Capacitor [capacitance=1μF package="100 mil [THT, tantalum]"]
  Part2 = Arduino Mega ADK (Rev3)

nets:
  N1: R1.Pin_0, R2.Pin_1, C1.+, Part2.A0
  N2: R2.Pin_0, Part2.D13_PWM
  N3: C1.-, Part2.GND
